# Fritzing sketch Expansão_Esp01 (saved by Fritzing 0.8.7b)
breadboards: 1

parts:
  ESP-1 = ESP-01 [part_number=ESP8266]
  MCP1 = MCP23016 [package="DIP (Dual Inline) [THT]"]
  Power_plug1 = Power plug
  R1 = Resistor [tolerance=±5% resistance=3.3 package=THT]
  C1 = Ceramic Capacitor [capacitance=10pF voltage=6.3V package="1206 [SMD, multilayer]"]
  U1 = 4RelayModule
  R2 = Resistor [tolerance=±5% resistance=3.3 package=THT]
  LED1 = LED - 5mm [color="Red (633nm)" package="5 mm [THT]"]
  U2 = 4RelayModule

nets:
  VCC: ESP-1.VCC, MCP1.VDD, Power_plug1.VCC, U1.VCC, U2.VCC
  GND: ESP-1.GND, MCP1.A0, MCP1.A1, MCP1.A2, MCP1.VSS#18, Power_plug1.GND, R1.Pin_1, C1.1, LED1.anode, U2.GND
  N1: ESP-1.GPIO0, MCP1.SDA
  N2: ESP-1.GPIO2, MCP1.SCL
  N3: MCP1.GP1.0, R2.Pin_0
  N4: MCP1.GP1.2, U2.IN4
  N5: MCP1.GP1.3, U2.IN3
  N6: MCP1.INT, U2.IN2
  N7: MCP1.GP1.4, U2.IN1
  N8: MCP1.CLK, R1.Pin_0, C1.0
  N9: MCP1.GP0.4, U1.IN4
  N10: MCP1.GP0.5, U1.IN3
  N11: MCP1.GP0.6, U1.IN2
  N12: MCP1.GP0.7, U1.IN1
  N13: R2.Pin_1, LED1.cathode

custom parts:
  ESP-01: ESP8266 Module, especifically the ESP-01.
  MCP23016: An I2C BUS 16 bit I/O expander.
  4RelayModule: 4 relay arduino module SONGLE SRD05VDC-SL-C
